// Logisim project disaster_warning_device.circ as structural Verilog: 12 circuits, main circuit flood_condition
module DEVICE (
  input  MODE,
  input  [6:0] _0_127__mm_hr,
  input  [4:0] in_3,
  input  [6:0] _0_127__kmph,
  input  [6:0] _0_127__cm
);

  wire cyclone_condition_1_cyclone, decoder_1_cyclone, decoder_1_earthquake, decoder_1_flood,
       decoder_1_tsunami, earthquake_condition_1_earthquake, flood_condition_1_flood, mode_logic_1_output,
       mode_logic_2_output, mode_logic_3_output, mode_logic_4_output, not_1_out, not_2_out,
       priority_encoder_1_safe_danger, tsunami_condition_1_tsunami;
  wire [1:0] priority_encoder_1_y1_y0, rain_1_r1r0, sea_level_1_l1l0, seismic_1_s1s0, wind_1_w1w0;

  rain rain_1 (.rain_input(_0_127__mm_hr), .r1r0(rain_1_r1r0));
  seismic seismic_1 (.seismic_input(in_3), .s1s0(seismic_1_s1s0));
  wind wind_1 (.wind_input(_0_127__kmph), .w1w0(wind_1_w1w0));
  sea_level sea_level_1 (.seal_level_input(_0_127__cm), .l1l0(sea_level_1_l1l0));
  flood_condition flood_condition_1 (
    .R1R0(rain_1_r1r0), .S1S0(seismic_1_s1s0), .W1W0(wind_1_w1w0), .L1L0(sea_level_1_l1l0),
    .FLOOD(flood_condition_1_flood));
  cyclone_condition cyclone_condition_1 (
    .R1R0(rain_1_r1r0), .S1S0(seismic_1_s1s0), .W1W0(wind_1_w1w0), .L1L0(sea_level_1_l1l0),
    .CYCLONE(cyclone_condition_1_cyclone));
  earthquake_condition earthquake_condition_1 (
    .R1R0(rain_1_r1r0), .S1S0(seismic_1_s1s0), .W1W0(wind_1_w1w0), .L1L0(sea_level_1_l1l0),
    .EARTHQUAKE(earthquake_condition_1_earthquake));
  Tsunami_condition tsunami_condition_1 (
    .R1R0(rain_1_r1r0), .S1S0(seismic_1_s1s0), .W1W0(wind_1_w1w0), .L1L0(sea_level_1_l1l0),
    .TSUNAMI(tsunami_condition_1_tsunami));
  not not_1 (not_1_out, MODE);
  priority_encoder priority_encoder_1 (
    .F(flood_condition_1_flood), .C(cyclone_condition_1_cyclone), .E(earthquake_condition_1_earthquake),
    .T(tsunami_condition_1_tsunami), .SAFE_DANGER(priority_encoder_1_safe_danger),
    .Y1_Y0(priority_encoder_1_y1_y0));
  not not_2 (not_2_out, priority_encoder_1_safe_danger);
  LED SAFE (.in(not_2_out));
  LED DANGER (.in(priority_encoder_1_safe_danger));
  decoder decoder_1 (
    .Safe_danger(priority_encoder_1_safe_danger), .Y1_Y0(priority_encoder_1_y1_y0), .FLOOD(decoder_1_flood),
    .CYCLONE(decoder_1_cyclone), .EARTHQUAKE(decoder_1_earthquake), .TSUNAMI(decoder_1_tsunami));
  mode_logic mode_logic_1 (
    .m(MODE), .Disaster_condition(flood_condition_1_flood), .Decoded_disaster(decoder_1_flood),
    .not_m(not_1_out), .OUTPUT(mode_logic_1_output));
  mode_logic mode_logic_2 (
    .m(MODE), .Disaster_condition(cyclone_condition_1_cyclone), .Decoded_disaster(decoder_1_cyclone),
    .not_m(not_1_out), .OUTPUT(mode_logic_2_output));
  mode_logic mode_logic_3 (
    .m(MODE), .Disaster_condition(earthquake_condition_1_earthquake),
    .Decoded_disaster(decoder_1_earthquake), .not_m(not_1_out), .OUTPUT(mode_logic_3_output));
  mode_logic mode_logic_4 (
    .m(MODE), .Disaster_condition(tsunami_condition_1_tsunami), .Decoded_disaster(decoder_1_tsunami),
    .not_m(not_1_out), .OUTPUT(mode_logic_4_output));
  LED FLOOD (.in(mode_logic_1_output));
  LED CYCLONE (.in(mode_logic_2_output));
  LED EARTHQUAKE (.in(mode_logic_3_output));
  LED TSUNAMI (.in(mode_logic_4_output));

  // Notes on the sheet:
  //   Rain
  //   rain input
  //   to 
  //   2-bit Binary
  //   seismic input
  //   to 
  //   2-bit Binary
  //   MODE 
  //   0
  //   1
  //   Seismic
  //   ((0.0-3.1)x10) kmph
  //   2-bit Binary
  //   INDEX
  //   TYPE
  //   UNIQUE DISASTER
  //   MULTI DISASTER
  //   Wind
  //   wind input
  //   to 
  //   Sea Level
  //   sea level input
  //   to 
  //   2-bit Binary
  //   0-2
  //   3-10
  //   11-30
  //   >= 31
  //   RAIN
  //   Flood Condition
  //   Cyclone Condition
  //   Earthquake Condition
  //   Tsunami Condition
  //   SEISMIC
  //   0-0.1
  //   0.2-0.5
  //   0.6-1.5
  //   >= 1.6
  //   DISASTER WARNING DEVICE
  //   WIND
  //   0-15
  //   16-30
  //   31-60
  //   >= 61
  //   SEA LEVEL
  //   0-5
  //   6-20
  //   21-50
  //   >= 51
  //   Priority Arrangement
  //   IMPACT
  //   Low/None
  //   Medium
  //   High
  //   Very High
  //   Decoded Disaster
  //   Mode Response
  //   PRIORITY
  //   Tsunami>Earthquake>Cyclone>Flood
endmodule

module flood_condition (
  input  [1:0] R1R0,
  input  [1:0] S1S0,
  input  [1:0] W1W0,
  input  [1:0] L1L0,
  output FLOOD
);

  wire and_1_out, comparator_1_eq, comparator_1_lt, comparator_2_eq, comparator_3_eq, comparator_3_gt,
       comparator_4_eq, comparator_4_gt, or_1_out, or_2_out, or_3_out, or_4_out;

  Comparator #(.width(2)) comparator_1 (.a(R1R0), .b(2'b10), .eq(comparator_1_eq), .lt(comparator_1_lt));  // open: gt
  Comparator #(.width(2)) comparator_2 (.a(R1R0), .b(2'b11), .eq(comparator_2_eq));  // open: gt, lt
  Comparator #(.width(2)) comparator_3 (.a(W1W0), .b(2'b10), .gt(comparator_3_gt), .eq(comparator_3_eq));  // open: lt
  Comparator #(.width(2)) comparator_4 (.a(L1L0), .b(2'b10), .gt(comparator_4_gt), .eq(comparator_4_eq));  // open: lt
  or or_1 (or_1_out, comparator_1_lt, comparator_1_eq);
  or or_2 (or_2_out, comparator_3_gt, comparator_3_eq);
  or or_3 (or_3_out, comparator_4_gt, comparator_4_eq);
  or or_4 (or_4_out, or_2_out, or_3_out);
  or or_5 (FLOOD, comparator_2_eq, and_1_out);
  and and_1 (and_1_out, or_1_out, or_4_out);

  // Notes on the sheet:
  //   Flood Condition:
  //    r1. (w1+l1+r0)
endmodule

module cyclone_condition (
  input  [1:0] R1R0,
  input  [1:0] S1S0,
  input  [1:0] W1W0,
  input  [1:0] L1L0,
  output CYCLONE
);

  wire and_1_out, comparator_1_eq, comparator_1_gt, comparator_2_eq, comparator_2_lt, comparator_3_eq,
       comparator_4_eq, comparator_4_gt, or_1_out, or_2_out, or_3_out, or_4_out;

  Comparator #(.width(2)) comparator_1 (.a(R1R0), .b(2'b10), .gt(comparator_1_gt), .eq(comparator_1_eq));  // open: lt
  Comparator #(.width(2)) comparator_2 (.a(W1W0), .b(2'b10), .eq(comparator_2_eq), .lt(comparator_2_lt));  // open: gt
  Comparator #(.width(2)) comparator_3 (.a(W1W0), .b(2'b11), .eq(comparator_3_eq));  // open: gt, lt
  Comparator #(.width(2)) comparator_4 (.a(L1L0), .b(2'b10), .gt(comparator_4_gt), .eq(comparator_4_eq));  // open: lt
  or or_1 (or_1_out, comparator_1_gt, comparator_1_eq);
  or or_2 (or_2_out, comparator_2_lt, comparator_2_eq);
  or or_3 (or_3_out, comparator_4_gt, comparator_4_eq);
  or or_4 (or_4_out, or_1_out, or_3_out);
  and and_1 (and_1_out, or_4_out, or_2_out);
  or or_5 (CYCLONE, and_1_out, comparator_3_eq);

  // Notes on the sheet:
  //   Cyclone Condition:
  //    w1.(w0+l1+r1)
endmodule

module earthquake_condition (
  input  [1:0] R1R0,
  input  [1:0] S1S0,
  input  [1:0] W1W0,
  input  [1:0] L1L0,
  output EARTHQUAKE
);

  or or_1 (EARTHQUAKE, S1S0[0], S1S0[1]);

  // Notes on the sheet:
  //   Earthquake Condition:
  //    s1+s0
endmodule

module Tsunami_condition (
  input  [1:0] R1R0,
  input  [1:0] S1S0,
  input  [1:0] W1W0,
  input  [1:0] L1L0,
  output TSUNAMI
);

  wire and_1_out;

  and and_1 (and_1_out, S1S0[0], S1S0[1]);
  or or_1 (TSUNAMI, and_1_out, L1L0[1]);

  // Notes on the sheet:
  //   Tsunami Condition:
  //    (s1.s0)+l1
endmodule

module mode_logic (
  input  m,
  input  Disaster_condition,
  input  Decoded_disaster,
  input  not_m,
  output OUTPUT
);

  wire and_1_out, and_2_out;

  and and_1 (and_1_out, m, Disaster_condition);
  and and_2 (and_2_out, Decoded_disaster, not_m);
  or or_1 (OUTPUT, and_1_out, and_2_out);

  // Notes on the sheet:
  //   Mode Response
endmodule

module priority_encoder (
  input  F,
  input  C,
  input  E,
  input  T,
  output SAFE_DANGER,
  output [1:0] Y1_Y0
);

  wire and_1_out, not_1_out, or_1_out;

  not not_1 (not_1_out, E);
  or or_1 (or_1_out, F, C);
  or or_2 (Y1_Y0[1], E, T);
  and and_1 (and_1_out, C, not_1_out);
  or or_3 (Y1_Y0[0], and_1_out, T);
  or or_4 (SAFE_DANGER, or_1_out, Y1_Y0[1]);

  // Notes on the sheet:
  //   Priority Encoder
endmodule

module decoder (
  input  Safe_danger,
  input  [1:0] Y1_Y0,
  output FLOOD,
  output CYCLONE,
  output EARTHQUAKE,
  output TSUNAMI
);

  wire not_1_out, not_2_out;

  not not_1 (not_1_out, Y1_Y0[1]);
  not not_2 (not_2_out, Y1_Y0[0]);
  and and_1 (FLOOD, not_1_out, Safe_danger, not_2_out);
  and and_2 (CYCLONE, not_1_out, Safe_danger, Y1_Y0[0]);
  and and_3 (EARTHQUAKE, Y1_Y0[1], Safe_danger, not_2_out);
  and and_4 (TSUNAMI, Y1_Y0[1], Safe_danger, Y1_Y0[0]);

  // Notes on the sheet:
  //   Decoder
endmodule

module rain (
  input  [6:0] rain_input,
  output [1:0] r1r0
);

  wire comparator_1_gt, comparator_2_gt, comparator_3_gt, comparator_4_eq, comparator_4_gt, or_1_out,
       xor_1_out;

  Comparator #(.mode("unsigned"), .width(7)) comparator_1 (
    .a(rain_input), .b(7'b0000010), .gt(comparator_1_gt));  // open: eq, lt
  Comparator #(.mode("unsigned"), .width(7)) comparator_2 (
    .a(rain_input), .b(7'b0001010), .gt(comparator_2_gt));  // open: eq, lt
  Comparator #(.mode("unsigned"), .width(7)) comparator_3 (
    .a(rain_input), .b(7'b0011110), .gt(comparator_3_gt));  // open: eq, lt
  Comparator #(.mode("unsigned"), .width(7)) comparator_4 (
    .a(rain_input), .b(7'b0011111), .gt(comparator_4_gt), .eq(comparator_4_eq));  // open: lt
  or or_1 (or_1_out, comparator_4_gt, comparator_4_eq);
  xor xor_1 (xor_1_out, comparator_1_gt, comparator_2_gt);
  or or_2 (r1r0[1], comparator_2_gt, comparator_3_gt);
  or or_3 (r1r0[0], xor_1_out, or_1_out);
endmodule

module seismic (
  input  [4:0] seismic_input,
  output [1:0] s1s0
);

  wire comparator_1_gt, comparator_2_gt, comparator_3_gt, comparator_4_eq, comparator_4_gt, or_1_out,
       xor_1_out;

  Comparator #(.mode("unsigned"), .width(5)) comparator_1 (
    .a(seismic_input), .b(5'b00001), .gt(comparator_1_gt));  // open: eq, lt
  Comparator #(.mode("unsigned"), .width(5)) comparator_2 (
    .a(seismic_input), .b(5'b00101), .gt(comparator_2_gt));  // open: eq, lt
  Comparator #(.mode("unsigned"), .width(5)) comparator_3 (
    .a(seismic_input), .b(5'b01110), .gt(comparator_3_gt));  // open: eq, lt
  Comparator #(.mode("unsigned"), .width(5)) comparator_4 (
    .a(seismic_input), .b(5'b10000), .gt(comparator_4_gt), .eq(comparator_4_eq));  // open: lt
  or or_1 (or_1_out, comparator_4_gt, comparator_4_eq);
  xor xor_1 (xor_1_out, comparator_1_gt, comparator_2_gt);
  or or_2 (s1s0[1], comparator_2_gt, comparator_3_gt);
  or or_3 (s1s0[0], xor_1_out, or_1_out);
endmodule

module wind (
  input  [6:0] wind_input,
  output [1:0] w1w0
);

  wire comparator_1_gt, comparator_2_gt, comparator_3_gt, comparator_4_eq, comparator_4_gt, or_1_out,
       xor_1_out;

  Comparator #(.mode("unsigned"), .width(7)) comparator_1 (
    .a(wind_input), .b(7'b0001111), .gt(comparator_1_gt));  // open: eq, lt
  Comparator #(.mode("unsigned"), .width(7)) comparator_2 (
    .a(wind_input), .b(7'b0011110), .gt(comparator_2_gt));  // open: eq, lt
  Comparator #(.mode("unsigned"), .width(7)) comparator_3 (
    .a(wind_input), .b(7'b0111100), .gt(comparator_3_gt));  // open: eq, lt
  Comparator #(.mode("unsigned"), .width(7)) comparator_4 (
    .a(wind_input), .b(7'b0111101), .gt(comparator_4_gt), .eq(comparator_4_eq));  // open: lt
  or or_1 (or_1_out, comparator_4_gt, comparator_4_eq);
  xor xor_1 (xor_1_out, comparator_1_gt, comparator_2_gt);
  or or_2 (w1w0[1], comparator_2_gt, comparator_3_gt);
  or or_3 (w1w0[0], xor_1_out, or_1_out);
endmodule

module sea_level (
  input  [6:0] seal_level_input,
  output [1:0] l1l0
);

  wire comparator_1_gt, comparator_2_gt, comparator_3_gt, comparator_4_eq, comparator_4_gt, or_1_out,
       xor_1_out;

  Comparator #(.mode("unsigned"), .width(7)) comparator_1 (
    .a(seal_level_input), .b(7'b0000101), .gt(comparator_1_gt));  // open: eq, lt
  Comparator #(.mode("unsigned"), .width(7)) comparator_2 (
    .a(seal_level_input), .b(7'b0010100), .gt(comparator_2_gt));  // open: eq, lt
  Comparator #(.mode("unsigned"), .width(7)) comparator_3 (
    .a(seal_level_input), .b(7'b0110010), .gt(comparator_3_gt));  // open: eq, lt
  Comparator #(.mode("unsigned"), .width(7)) comparator_4 (
    .a(seal_level_input), .b(7'b0110011), .gt(comparator_4_gt), .eq(comparator_4_eq));  // open: lt
  or or_1 (or_1_out, comparator_4_gt, comparator_4_eq);
  xor xor_1 (xor_1_out, comparator_1_gt, comparator_2_gt);
  or or_2 (l1l0[1], comparator_2_gt, comparator_3_gt);
  or or_3 (l1l0[0], xor_1_out, or_1_out);
endmodule
